// Logisim project Blatt04.circ as structural Verilog: 1 circuit, main circuit main
module main (
  output out_1,
  output out_2,
  output out_3,
  output out_4,
  output out_5,
  output out_6
);

  wire and_1_out, and_2_out, and_3_out, and_4_out, and_5_out, and_6_out, and_7_out, and_8_out, and_9_out,
       and_11_out, and_12_out, and_13_out, and_14_out, and_15_out, and_16_out, and_17_out, and_18_out,
       clock_1_out, d_ff_1_q, d_ff_2_q, d_ff_3_q, d_ff_4_q, not_2_out, not_3_out, not_4_out, or_4_out,
       or_5_out, or_6_out, or_7_out, or_8_out, or_10_out;

  not not_1 (out_4, d_ff_4_q);
  not not_2 (not_2_out, d_ff_3_q);
  not not_3 (not_3_out, d_ff_2_q);
  not not_4 (not_4_out, d_ff_1_q);
  and and_1 (and_1_out, out_4, d_ff_1_q);
  and and_2 (and_2_out, not_2_out, d_ff_1_q);
  or or_1 (out_1, and_1_out, and_2_out, and_3_out, and_4_out);
  Clock clock_1 (.out(clock_1_out));
  and and_3 (and_3_out, not_3_out, d_ff_1_q);
  D_Flip_Flop d_ff_1 (.D(out_1), .clk(clock_1_out), .Q(d_ff_1_q));  // open: Qn, preset, reset
  and and_4 (and_4_out, d_ff_4_q, d_ff_3_q, d_ff_2_q, not_4_out);
  and and_5 (and_5_out, out_4, d_ff_2_q);
  and and_6 (and_6_out, d_ff_4_q, not_3_out, d_ff_3_q);
  or or_2 (out_2, and_5_out, and_6_out, and_7_out);
  and and_7 (and_7_out, not_2_out, d_ff_2_q);
  D_Flip_Flop d_ff_2 (.D(out_2), .clk(clock_1_out), .Q(d_ff_2_q));  // open: Qn, preset, reset
  and and_8 (and_8_out, d_ff_4_q, not_2_out);
  and and_9 (and_9_out, out_4, d_ff_3_q);
  or or_3 (out_3, and_8_out, and_9_out);
  D_Flip_Flop d_ff_3 (.D(out_3), .clk(clock_1_out), .Q(d_ff_3_q));  // open: Qn, preset, reset
  D_Flip_Flop d_ff_4 (.D(out_4), .clk(clock_1_out), .Q(d_ff_4_q));  // open: Qn, preset, reset
  or or_4 (or_4_out, d_ff_4_q, d_ff_2_q);
  or or_5 (or_5_out, d_ff_3_q, d_ff_1_q);
  or or_6 (or_6_out, out_4, not_3_out);
  and and_10 (out_5, or_4_out, or_5_out, or_6_out, or_7_out);
  or or_7 (or_7_out, not_2_out, not_4_out);
  and and_11 (and_11_out, d_ff_4_q, not_2_out, not_3_out, not_4_out);
  and and_12 (and_12_out, out_4, d_ff_3_q, not_3_out, not_4_out);
  or or_8 (or_8_out, and_11_out, and_12_out, and_13_out, and_14_out);
  and and_13 (and_13_out, out_4, not_2_out, d_ff_2_q, not_4_out);
  and and_14 (and_14_out, d_ff_4_q, d_ff_3_q, d_ff_2_q, not_4_out);
  or or_9 (out_6, or_8_out, or_10_out);
  and and_15 (and_15_out, out_4, not_2_out, not_3_out, d_ff_1_q);
  and and_16 (and_16_out, d_ff_4_q, d_ff_3_q, not_3_out, d_ff_1_q);
  or or_10 (or_10_out, and_15_out, and_16_out, and_17_out, and_18_out);
  and and_17 (and_17_out, d_ff_4_q, not_2_out, d_ff_2_q, d_ff_1_q);
  and and_18 (and_18_out, out_4, d_ff_3_q, d_ff_2_q, d_ff_1_q);
  Clock clock_2 ();  // open: out
endmodule
