// Logisim project Blatt06_2.3_2.4_2.5.circ as structural Verilog: 1 circuit, main circuit main
module main (
  input  T,
  input  D,
  input  C,
  input  in_4,
  input  D_2,
  input  C_2,
  input  in_7,
  output Q1,
  output Q2,
  output Q2_2,
  output NOT_Q2,
  output Q2_3,
  output NOT_Q2_2
);

  wire j_k_ff_1_q, j_k_ff_1_qn, nand_1_out, nand_2_out, nand_3_out, nand_4_out, nand_5_out, nand_6_out,
       nand_7_out, nand_8_out, nand_9_out, nand_10_out, nand_11_out, nand_12_out, not_1_out, not_2_out,
       not_3_out, not_4_out, not_5_out, not_6_out, not_7_out;

  J_K_Flip_Flop j_k_ff_1 (.J(Q2), .K(Q1), .clk(T), .Q(j_k_ff_1_q), .Qn(j_k_ff_1_qn));  // open: preset, reset
  not not_1 (not_1_out, D);
  not not_2 (not_2_out, D_2);
  not not_3 (not_3_out, T);
  nand nand_1 (nand_1_out, D, C);
  nand nand_2 (nand_2_out, C, not_1_out);
  nand nand_3 (nand_3_out, D_2, C_2);
  nand nand_4 (nand_4_out, C_2, not_2_out);
  J_K_Flip_Flop j_k_ff_2 (.J(j_k_ff_1_q), .K(j_k_ff_1_qn), .clk(not_3_out), .Q(Q1), .Qn(Q2));  // open: preset, reset
  not not_4 (not_4_out, in_4);
  not not_5 (not_5_out, in_7);
  nand nand_5 (nand_5_out, nand_1_out, nand_6_out);
  nand nand_6 (nand_6_out, nand_5_out, nand_2_out);
  not not_6 (not_6_out, C);
  nand nand_7 (nand_7_out, nand_3_out, not_4_out, nand_8_out);
  nand nand_8 (nand_8_out, nand_7_out, not_5_out, nand_4_out);
  not not_7 (not_7_out, C_2);
  nand nand_9 (nand_9_out, nand_5_out, not_6_out);
  nand nand_10 (nand_10_out, not_6_out, nand_6_out);
  nand nand_11 (nand_11_out, nand_7_out, not_7_out);
  nand nand_12 (nand_12_out, not_7_out, nand_8_out);
  nand nand_13 (Q2_2, nand_9_out, NOT_Q2);
  nand nand_14 (NOT_Q2, Q2_2, nand_10_out);
  nand nand_15 (Q2_3, nand_11_out, NOT_Q2_2);
  nand nand_16 (NOT_Q2_2, Q2_3, nand_12_out);

  // Notes on the sheet:
  //   Aufgabe 2.3
  //   Aufgabe 2.4
  //   Aufgabe 2.5
  //   Preset
  //   Reset
  //   Q1
  //   NOT Q1
  //   Q1
  //   NOT Q1
endmodule
