// Logisim project Blatt07_1_2.3_2.4.circ as structural Verilog: 1 circuit, main circuit main
module main (
  input  in_1,
  output out_2,
  output out_3,
  output out_4,
  output out_5,
  output out_6,
  output out_7,
  output D1neu,
  output D2neu,
  output D3neu,
  output D4neu,
  output A,
  output B,
  output C,
  output D,
  output E,
  output F,
  output G
);

  wire and_1_out, and_2_out, and_3_out, and_4_out, and_5_out, and_6_out, and_7_out, and_8_out, and_9_out,
       and_10_out, and_11_out, and_12_out, and_13_out, and_14_out, and_15_out, and_16_out, and_17_out,
       and_18_out, and_19_out, and_20_out, and_21_out, and_22_out, and_23_out, and_24_out, and_25_out,
       and_26_out, and_27_out, and_28_out, and_29_out, and_30_out, and_31_out, and_32_out, and_33_out,
       and_34_out, and_35_out, clock_1_out, clock_2_out, d_ff_1_q, d_ff_1_qn, d_ff_2_q, d_ff_2_qn, d_ff_3_q,
       d_ff_3_qn, d_ff_4_q, d_ff_4_qn, d_ff_6_qn, j_k_ff_1_qn, not_2_out, not_3_out, not_4_out, s_r_ff_1_qn,
       s_r_ff_2_qn;

  not not_1 (D4neu, d_ff_4_q);
  not not_2 (not_2_out, d_ff_3_q);
  not not_3 (not_3_out, d_ff_2_q);
  not not_4 (not_4_out, d_ff_1_q);
  and and_1 (and_1_out, d_ff_1_q, not_3_out);
  and and_2 (and_2_out, d_ff_1_q, not_2_out);
  and and_3 (and_3_out, d_ff_2_q, not_2_out, d_ff_4_q);
  or or_1 (D1neu, and_1_out, and_2_out, and_3_out, and_4_out);
  Clock clock_1 (.out(clock_1_out));
  and and_4 (and_4_out, not_4_out, d_ff_2_q, d_ff_3_q, D4neu);
  D_Flip_Flop d_ff_1 (.D(D1neu), .clk(clock_1_out), .Q(d_ff_1_q), .Qn(d_ff_1_qn));  // open: preset, reset
  and and_5 (and_5_out, not_3_out, d_ff_3_q);
  and and_6 (and_6_out, not_3_out, d_ff_4_q);
  or or_2 (D2neu, and_5_out, and_6_out, and_7_out);
  and and_7 (and_7_out, d_ff_2_q, not_2_out, D4neu);
  D_Flip_Flop d_ff_2 (.D(D2neu), .clk(clock_1_out), .Q(d_ff_2_q), .Qn(d_ff_2_qn));  // open: preset, reset
  and and_8 (and_8_out, not_2_out, D4neu);
  and and_9 (and_9_out, not_3_out, d_ff_3_q, d_ff_4_q);
  or or_3 (D3neu, and_8_out, and_9_out, and_10_out);
  and and_10 (and_10_out, d_ff_1_q, d_ff_3_q, d_ff_4_q);
  D_Flip_Flop d_ff_3 (.D(D3neu), .clk(clock_1_out), .Q(d_ff_3_q), .Qn(d_ff_3_qn));  // open: preset, reset
  D_Flip_Flop d_ff_4 (.D(D4neu), .clk(clock_1_out), .Q(d_ff_4_q), .Qn(d_ff_4_qn));  // open: preset, reset
  Clock clock_2 (.out(clock_2_out));
  D_Flip_Flop d_ff_5 (.D(in_1), .clk(clock_2_out), .Q(out_2));  // open: Qn, preset, reset
  and and_11 (and_11_out, d_ff_4_q, d_ff_3_q, d_ff_1_q);
  D_Flip_Flop d_ff_6 (.D(out_2), .clk(clock_2_out), .Q(out_3), .Qn(d_ff_6_qn));  // open: preset, reset
  and and_12 (and_12_out, d_ff_4_qn, d_ff_3_q, d_ff_2_q, d_ff_1_qn);
  or or_4 (A, and_11_out, and_12_out);
  and and_13 (and_13_out, d_ff_4_q, d_ff_2_q, d_ff_1_q);
  S_R_Flip_Flop s_r_ff_1 (
    .S(out_3), .R(d_ff_6_qn), .clk(clock_2_out), .Q(out_4), .Qn(s_r_ff_1_qn));  // open: reset, preset
  and and_14 (and_14_out, d_ff_4_qn, d_ff_2_qn, d_ff_1_q);
  or or_5 (B, and_13_out, and_14_out, and_15_out, and_16_out);
  S_R_Flip_Flop s_r_ff_2 (
    .S(out_4), .R(s_r_ff_1_qn), .clk(clock_2_out), .Q(out_5), .Qn(s_r_ff_2_qn));  // open: reset, preset
  and and_15 (and_15_out, d_ff_2_qn, d_ff_3_q, d_ff_4_q);
  J_K_Flip_Flop j_k_ff_1 (
    .J(out_5), .K(s_r_ff_2_qn), .clk(clock_2_out), .Q(out_6), .Qn(j_k_ff_1_qn));  // open: preset, reset
  and and_16 (and_16_out, d_ff_4_qn, d_ff_3_qn, d_ff_2_q, d_ff_1_qn);
  J_K_Flip_Flop j_k_ff_2 (.J(out_6), .K(j_k_ff_1_qn), .clk(clock_2_out), .Q(out_7));  // open: Qn, preset, reset
  and and_17 (and_17_out, d_ff_4_q, d_ff_2_q, d_ff_1_q);
  and and_18 (and_18_out, d_ff_4_qn, d_ff_2_qn, d_ff_1_q);
  and and_19 (and_19_out, d_ff_2_qn, d_ff_3_q, d_ff_4_q);
  or or_6 (C, and_17_out, and_18_out, and_19_out, and_20_out);
  and and_20 (and_20_out, d_ff_1_qn, d_ff_2_q, d_ff_3_qn);
  and and_21 (and_21_out, d_ff_4_q, d_ff_1_q);
  and and_22 (and_22_out, d_ff_4_q, d_ff_3_qn);
  and and_23 (and_23_out, d_ff_3_qn, d_ff_1_q);
  or or_7 (D, and_21_out, and_22_out, and_23_out, and_24_out);
  _7_Segment_Display u_7_segment_display_1 (.g(G), .f(F), .a(A), .b(B), .e(E), .d(D), .c(C));  // open: dp
  and and_24 (and_24_out, d_ff_4_qn, d_ff_2_q, d_ff_1_qn);
  Clock Takt ();  // open: out
  and and_25 (and_25_out, d_ff_4_q, d_ff_1_q);
  and and_26 (and_26_out, d_ff_3_qn, d_ff_1_qn);
  or or_8 (E, and_25_out, and_26_out, and_27_out);
  and and_27 (and_27_out, d_ff_4_qn, d_ff_2_q);
  and and_28 (and_28_out, d_ff_4_q, d_ff_1_q);
  and and_29 (and_29_out, d_ff_4_q, d_ff_3_qn);
  and and_30 (and_30_out, d_ff_3_qn, d_ff_2_qn, d_ff_1_qn);
  or or_9 (F, and_28_out, and_29_out, and_30_out, and_31_out, and_32_out);
  and and_31 (and_31_out, d_ff_3_qn, d_ff_2_q, d_ff_1_q);
  and and_32 (and_32_out, d_ff_4_qn, d_ff_3_q, d_ff_2_q, d_ff_1_qn);
  and and_33 (and_33_out, d_ff_4_qn, d_ff_3_q, d_ff_2_q);
  and and_34 (and_34_out, d_ff_4_qn, d_ff_3_qn, d_ff_1_qn);
  or or_10 (G, and_33_out, and_34_out, and_35_out);
  and and_35 (and_35_out, d_ff_4_q, d_ff_3_q, d_ff_2_qn, d_ff_1_qn);

  // Notes on the sheet:
  //   Aufgabe 2.3
  //   Aufgabe 1
  //   Aufgabe 2.4
endmodule
