// Logisim project Blatt11.circ as structural Verilog: 1 circuit, main circuit main
module main (
  input  C,
  input  A,
  input  in_3,
  input  B,
  input  A_2,
  input  C_2,
  input  A_3,
  input  B_2,
  input  C_3
);

  wire pull_resistor_1_node, pull_resistor_3_node, pull_resistor_10_node, pull_resistor_13_node,
       pull_resistor_15_node, pull_resistor_16_node, transistor_2_out, transistor_3_out, transistor_5_out,
       transistor_6_out, transistor_9_out, transistor_10_out, transistor_11_out, transistor_12_out,
       transistor_13_out, transistor_15_out, transistor_18_out, transistor_19_out, transistor_20_out,
       transistor_21_out, transistor_22_out, transistor_27_out, transistor_28_out, transistor_31_out,
       transistor_33_out, transistor_34_out, transistor_37_out, transistor_38_out, transistor_39_out,
       transistor_43_out, transistor_44_out, transistor_48_out;

  Pull_Resistor #(.pull(1)) pull_resistor_1 (.node(pull_resistor_1_node));
  Transistor #(.\type ("n")) transistor_1 (.in(1'b0), .out(pull_resistor_1_node), .gate(A));
  Transistor #(.\type ("n")) transistor_2 (.in(1'b0), .out(transistor_2_out), .gate(pull_resistor_1_node));
  Transistor transistor_3 (.in(1'b1), .out(transistor_3_out), .gate(A_2));
  Pull_Resistor pull_resistor_2 (.node(transistor_3_out));
  Pull_Resistor #(.pull(1)) pull_resistor_3 (.node(pull_resistor_3_node));
  Pull_Resistor #(.pull(1)) pull_resistor_4 (.node(transistor_2_out));
  Transistor #(.\type ("n")) transistor_4 (.in(1'b0), .out(pull_resistor_3_node), .gate(C));
  Transistor transistor_5 (.in(1'b1), .out(transistor_5_out), .gate(C_2));
  Pull_Resistor pull_resistor_5 (.node(transistor_5_out));
  Transistor transistor_6 (.in(1'b1), .out(transistor_6_out), .gate(A_3));
  Transistor #(.\type ("n")) transistor_7 (.in(1'b0), .out(transistor_6_out), .gate(A_3));
  Transistor #(.\type ("n")) transistor_8 (.in(1'b0), .out(transistor_2_out), .gate(C));
  Transistor transistor_9 (.in(1'b1), .out(transistor_9_out), .gate(transistor_3_out));
  Transistor transistor_10 (.in(transistor_9_out), .out(transistor_10_out), .gate(C_2));
  Pull_Resistor pull_resistor_6 (.node(transistor_10_out));
  Transistor #(.\type ("n")) transistor_11 (.in(1'b0), .out(transistor_11_out), .gate(pull_resistor_3_node));
  Transistor transistor_12 (.in(1'b1), .out(transistor_12_out), .gate(transistor_10_out));
  Pull_Resistor pull_resistor_7 (.node(transistor_12_out));
  Transistor transistor_13 (.in(1'b1), .out(transistor_13_out), .gate(C_3));
  Transistor #(.\type ("n")) transistor_14 (.in(1'b0), .out(transistor_13_out), .gate(C_3));
  Pull_Resistor #(.pull(1)) pull_resistor_8 (.node(transistor_11_out));
  Transistor transistor_15 (.in(1'b1), .out(transistor_15_out), .gate(B));
  Pull_Resistor pull_resistor_9 (.node(transistor_15_out));
  Pull_Resistor #(.pull(1)) pull_resistor_10 (.node(pull_resistor_10_node));
  Transistor #(.\type ("n")) transistor_16 (.in(1'b0), .out(pull_resistor_10_node), .gate(transistor_2_out));
  Transistor #(.\type ("n")) transistor_17 (.in(1'b0), .out(transistor_11_out), .gate(A));
  Transistor #(.\type ("n")) transistor_18 (.in(1'b0), .out(transistor_18_out), .gate(transistor_6_out));
  Transistor transistor_19 (.in(1'b1), .out(transistor_19_out), .gate(A_2));
  Transistor transistor_20 (.in(transistor_19_out), .out(transistor_20_out), .gate(transistor_15_out));
  Transistor transistor_21 (.in(transistor_20_out), .out(transistor_21_out), .gate(transistor_5_out));
  Pull_Resistor pull_resistor_11 (.node(transistor_21_out));
  Transistor transistor_22 (.in(1'b1), .out(transistor_22_out), .gate(transistor_6_out));
  Transistor transistor_23 (.in(transistor_22_out), .out(transistor_18_out), .gate(C_3));
  Transistor #(.\type ("n")) transistor_24 (.in(1'b0), .out(transistor_18_out), .gate(C_3));
  Pull_Resistor #(.pull(1)) pull_resistor_12 (.node(transistor_11_out));
  Pull_Resistor #(.pull(1)) pull_resistor_13 (.node(pull_resistor_13_node));
  Transistor #(.\type ("n")) transistor_25 (.in(1'b0), .out(transistor_11_out), .gate(pull_resistor_13_node));
  Transistor #(.\type ("n")) transistor_26 (.in(1'b0), .out(pull_resistor_13_node), .gate(in_3));
  Transistor transistor_27 (.in(1'b1), .out(transistor_27_out), .gate(transistor_21_out));
  Pull_Resistor pull_resistor_14 (.node(transistor_27_out));
  Transistor transistor_28 (.in(1'b1), .out(transistor_28_out), .gate(transistor_18_out));
  Transistor #(.\type ("n")) transistor_29 (.in(1'b0), .out(transistor_28_out), .gate(transistor_18_out));
  Pull_Resistor #(.pull(1)) pull_resistor_15 (.node(pull_resistor_15_node));
  Transistor #(.\type ("n")) transistor_30 (.in(1'b0), .out(pull_resistor_15_node), .gate(transistor_11_out));
  Transistor transistor_31 (.in(1'b1), .out(transistor_31_out), .gate(transistor_27_out));
  Pull_Resistor #(.pull(1)) pull_resistor_16 (.node(pull_resistor_16_node));
  LED led_1 (.in(pull_resistor_16_node));
  Transistor #(.\type ("n")) transistor_32 (
    .in(transistor_33_out), .out(pull_resistor_16_node), .gate(pull_resistor_10_node));
  Transistor #(.\type ("n")) transistor_33 (.in(1'b0), .out(transistor_33_out), .gate(pull_resistor_15_node));
  Pull_Resistor pull_resistor_17 (.node(transistor_31_out));
  Transistor transistor_34 (.in(1'b1), .out(transistor_34_out), .gate(B_2));
  Transistor #(.\type ("n")) transistor_35 (.in(1'b0), .out(transistor_34_out), .gate(B_2));
  Transistor transistor_36 (.in(1'b1), .out(transistor_31_out), .gate(transistor_12_out));
  LED led_2 (.in(transistor_31_out));
  Transistor transistor_37 (.in(1'b1), .out(transistor_37_out), .gate(A_3));
  Transistor transistor_38 (.in(transistor_37_out), .out(transistor_38_out), .gate(transistor_34_out));
  Transistor transistor_39 (.in(transistor_38_out), .out(transistor_39_out), .gate(transistor_13_out));
  Transistor #(.\type ("n")) transistor_40 (.in(1'b0), .out(transistor_39_out), .gate(transistor_34_out));
  Transistor #(.\type ("n")) transistor_41 (.in(1'b0), .out(transistor_39_out), .gate(A_3));
  Transistor #(.\type ("n")) transistor_42 (.in(1'b0), .out(transistor_39_out), .gate(transistor_13_out));
  Transistor transistor_43 (.in(1'b1), .out(transistor_43_out), .gate(transistor_44_out));
  Transistor transistor_44 (.in(1'b1), .out(transistor_44_out), .gate(transistor_39_out));
  Transistor #(.\type ("n")) transistor_45 (.in(1'b0), .out(transistor_44_out), .gate(transistor_39_out));
  Transistor transistor_46 (.in(1'b1), .out(transistor_43_out), .gate(transistor_28_out));
  LED led_3 (.in(transistor_43_out));
  Transistor #(.\type ("n")) transistor_47 (.in(transistor_48_out), .out(transistor_43_out), .gate(transistor_44_out));
  Transistor #(.\type ("n")) transistor_48 (.in(1'b0), .out(transistor_48_out), .gate(transistor_28_out));

  // Notes on the sheet:
  //   Aufgabe 3.2 - PMOS Transistorschaltung
  //   Aufgabe 3.1 - NMOS Transistorschaltung
  //   B
  //   f
  //   f
endmodule
