// Logisim project Comparator.circ as structural Verilog: 1 circuit, main circuit main
module main (
  input  x0,
  input  x1,
  input  y0,
  input  y1,
  output y_equals_x,
  output y_less_than_x,
  output y_greater_than_x
);

  wire and_1_out, and_2_out, and_3_out, and_4_out, and_5_out, and_6_out, and_7_out, and_8_out, and_9_out,
       and_10_out, not_1_out, not_2_out, not_3_out, not_4_out;

  not not_1 (not_1_out, x0);
  not not_2 (not_2_out, x1);
  not not_3 (not_3_out, y0);
  not not_4 (not_4_out, y1);
  and and_1 (and_1_out, x0, x1, y0, y1);
  and and_2 (and_2_out, x0, not_2_out, y0, not_4_out);
  or or_1 (y_equals_x, and_1_out, and_2_out, and_3_out, and_4_out);
  and and_3 (and_3_out, not_1_out, x1, not_3_out, y1);
  and and_4 (and_4_out, not_1_out, not_2_out, not_3_out, not_4_out);
  and and_5 (and_5_out, x1, not_4_out);
  and and_6 (and_6_out, x0, x1, not_3_out);
  or or_2 (y_less_than_x, and_5_out, and_6_out, and_7_out);
  and and_7 (and_7_out, x0, not_3_out, not_4_out);
  and and_8 (and_8_out, not_2_out, y1);
  and and_9 (and_9_out, not_1_out, not_2_out, y0);
  or or_3 (y_greater_than_x, and_8_out, and_9_out, and_10_out);
  and and_10 (and_10_out, not_1_out, y0, y1);
endmodule
