// Logisim project Full-Adder.circ as structural Verilog: 1 circuit, main circuit main
module main (
  input  x,
  input  y,
  input  c_in,
  output c_out,
  output s
);

  wire and_1_out, and_2_out, xor_1_out;

  and and_1 (and_1_out, x, y);
  xor xor_1 (xor_1_out, x, y);
  and and_2 (and_2_out, xor_1_out, c_in);
  or or_1 (c_out, and_1_out, and_2_out);
  xor xor_2 (s, xor_1_out, c_in);
endmodule
