// Logisim project GreyCode.circ as structural Verilog: 1 circuit, main circuit main
module main (
  output out_1,
  output out_2,
  output out_3
);

  wire and_1_out, and_2_out, and_3_out, and_4_out, and_5_out, and_6_out, clock_1_out, clock_2_out,
       clock_3_out, d_ff_1_q, d_ff_2_q, d_ff_3_q, not_1_out, not_2_out, not_3_out;

  not not_1 (not_1_out, d_ff_3_q);
  not not_2 (not_2_out, d_ff_2_q);
  not not_3 (not_3_out, d_ff_1_q);
  and and_1 (and_1_out, d_ff_1_q, d_ff_3_q);
  and and_2 (and_2_out, d_ff_2_q, not_1_out);
  or or_1 (out_1, and_1_out, and_2_out);
  Clock clock_1 (.out(clock_1_out));
  and and_3 (and_3_out, not_3_out, d_ff_3_q);
  D_Flip_Flop d_ff_1 (.D(out_1), .clk(clock_1_out), .Q(d_ff_1_q));  // open: Qn, preset, reset
  and and_4 (and_4_out, d_ff_2_q, not_1_out);
  or or_2 (out_2, and_3_out, and_4_out);
  Clock clock_2 (.out(clock_2_out));
  and and_5 (and_5_out, d_ff_1_q, d_ff_2_q);
  D_Flip_Flop d_ff_2 (.D(out_2), .clk(clock_2_out), .Q(d_ff_2_q));  // open: Qn, preset, reset
  and and_6 (and_6_out, not_3_out, not_2_out);
  or or_3 (out_3, and_5_out, and_6_out);
  Clock clock_3 (.out(clock_3_out));
  D_Flip_Flop d_ff_3 (.D(out_3), .clk(clock_3_out), .Q(d_ff_3_q));  // open: Qn, preset, reset
endmodule
