// Logisim project Multiplication.circ as structural Verilog: 1 circuit, main circuit main
module main (
  input  b2,
  input  b1,
  input  a2,
  input  a1,
  output x3,
  output x2,
  output x1,
  output x0
);

  wire and_2_out, and_3_out, and_4_out, and_5_out, and_6_out, and_7_out, not_1_out, not_2_out, not_3_out,
       not_4_out;

  not not_1 (not_1_out, b2);
  not not_2 (not_2_out, b1);
  not not_3 (not_3_out, a2);
  not not_4 (not_4_out, a1);
  and and_1 (x3, b2, b1, a2, a1);
  and and_2 (and_2_out, b2, not_2_out, a2);
  and and_3 (and_3_out, b2, a2, not_4_out);
  or or_1 (x2, and_2_out, and_3_out);
  and and_4 (and_4_out, not_1_out, b1, a2);
  and and_5 (and_5_out, b2, not_2_out, a1);
  and and_6 (and_6_out, b2, not_3_out, a1);
  or or_2 (x1, and_4_out, and_5_out, and_6_out, and_7_out);
  and and_7 (and_7_out, b1, a2, not_4_out);
  and and_8 (x0, b1, a1);
endmodule
