// Logisim project MOS_Inverter.circ as structural Verilog: 1 circuit, main circuit main
module main (
  input  a_1,
  input  a_2,
  input  a_3,
  output y_1,
  output y_3,
  output y_2
);

  Pull_Resistor #(.pull(1)) pull_resistor_1 (.node(y_1));
  Transistor #(.\type ("n")) transistor_1 (.in(1'b0), .out(y_1), .gate(a_1));
  Transistor transistor_2 (.in(1'b1), .out(y_2), .gate(a_2));
  Pull_Resistor pull_resistor_2 (.node(y_2));
  Transistor transistor_3 (.in(1'b1), .out(y_3), .gate(a_3));
  Transistor #(.\type ("n")) transistor_4 (.in(1'b0), .out(y_3), .gate(a_3));

  // Notes on the sheet:
  //   NMOS Inverter
  //   PMOS Inverter
  //   CMOS Inverter
endmodule
